# Fritzing sketch wiring-diagram (saved by Fritzing 0.9.4)

parts:
  part = Arduino Mini (Rev5)
  part_2 = Bluetooth HC-05 Macho
  BMP180 = Barometric Pressure Sensor - BMP180 Breakout (GY-68)
  Töltés = TP4056 [chip_label=TP4056 package="DIP (Dual Inline) [THT]"]
  Főkapcsoló = Toggle Switch [package=THT]
  BAT = Battery
  part_3 = 4-Line Bi-Directional Level Shifter
  5V_to_3_5V = DC_DC_XL4016 [package=board_screw]
  BAT_LED = smd LED [color="Red (633nm)" package="0805 [SMD]"]
  ERROR_LED = smd LED [color="Blue (470nm)" package="0805 [SMD]"]
  BAT_fesz_mérő = INA219 DC Current Sensor Breakout
  R1 = Resistor [tolerance=±5% resistance=220 package=THT]

nets:
  N1: part.D0/TX, part.TX, part_3.A4
  N2: part.D1/RX, part_2.TXD
  N3: part.GND, part_3.GND#6, R1.Pin_0
  N4: part.D2, BAT_LED.anode
  N5: part.D3_PWM, ERROR_LED.anode
  5V: part.5V, Főkapcsoló.COM, 5V_to_3_5V.IN+, BAT_fesz_mérő.VCC
  N6: part.A4, BMP180.SDA, BAT_fesz_mérő.SDA
  N7: part.A5, BMP180.SCL, BAT_fesz_mérő.SCL
  N8: part_2.RXD, part_3.B4
  N9: part_2.GND, part_3.GND#16
  N10: BMP180.VCC, 5V_to_3_5V.OUT+
  N11: BMP180.GND, 5V_to_3_5V.OUT-
  N12: Töltés.pin3, Főkapcsoló.L2
  N13: Töltés.pin4, BAT_fesz_mérő.Vin+
  N14: Töltés.pin5, BAT.-
  N15: Töltés.pin6, 5V_to_3_5V.IN-, BAT_fesz_mérő.GND
  N16: BAT.+, BAT_fesz_mérő.Vin-
  N17: BAT_LED.cathode, ERROR_LED.cathode, R1.Pin_1

custom parts:
  TP4056: A DIP stand-in part for whatever IC you want. With 6 pins on a 300mil dual inline package (DIP) footprint.
  4-Line Bi-Directional Level Shifter: 4-Channel Bi-Directional Level Shifter
  INA219 DC Current Sensor Breakout: INA DC Current Sensor Breakout
